# Fritzing sketch GOT_Raspberry (saved by Fritzing 0.9.2b)
breadboards: 1

parts:
  T1 = DS1822 Temperature Sensor [package="TO92 [THT]"]
  R3 = PHOTOCELL [package=photocell]
  DHT1 = DHT22 Humidity and Temperature Sensor
  U1 = HIH-4030 [package=hih-4030]
  R2 = Resistor [tolerance=±5% resistance=220 package="0402 [SMD]"]
  R4 = Resistor [tolerance=±5% resistance=4.7k package=THT]
  R5 = Resistor [tolerance=±5% resistance=4.7k package=THT]
  R6 = Resistor [tolerance=±5% resistance=4.7k package=THT]
  Raspberry_Pi2 = Raspberry Pi B rev2
  IC1 = MCP3008 8-channel 10-bit ADC [part_number=MCP3008]

nets (from the schematic view):
  VDD: T1.+Vdd, DHT1.VDD, R2.Pin_1, R4.Pin_0, Raspberry_Pi2.3V3, IC1.no_name_yet#15, IC1.no_name_yet#16
  N1: T1.DQ, Raspberry_Pi2.GPIO_17
  GND: T1.GND, R3.P$2, DHT1.GND, U1.GND, R6.Pin_0, IC1.no_name_yet#9, IC1.no_name_yet#14
  N2: R3.P$1, R2.Pin_0, IC1.no_name_yet#2
  N3: DHT1.DATA, Raspberry_Pi2.GPIO_4
  N4: U1.OUT, R5.Pin_0, R6.Pin_1, IC1.no_name_yet#1
  VCC: U1.VCC, R5.Pin_1, Raspberry_Pi2.5V
  N5: Raspberry_Pi2.GPIO_10, IC1.no_name_yet#11
  N6: Raspberry_Pi2.GPIO_9, IC1.no_name_yet#12
  N7: Raspberry_Pi2.GPIO_11, IC1.no_name_yet#13
  N8: Raspberry_Pi2.GPIO_8, IC1.no_name_yet#10

custom parts:
  DS1822 Temperature Sensor: A DS1822 temperature sensor with a temperature range from -55°C to 150°C. Digital, 1-wire bus.
